// Digital circuit abs_difference.dig as structural Verilog
module abs_difference (
  input  a_0,
  input  a_1,
  input  b_0,
  input  b_1,
  output y_0,
  output y_1
);

  wire add_1_c_o, add_1_s, add_2_c_o, add_2_s, add_3_c_o, not_1_out, not_2_out, not_3_out, xor_1_out,
       xor_2_out;

  not not_1 (not_1_out, b_0);
  not not_2 (not_2_out, b_1);
  Add add_1 (.a(a_0), .b(not_1_out), .c_i(1'b1), .s(add_1_s), .c_o(add_1_c_o));
  Add add_2 (.a(a_1), .b(not_2_out), .c_i(add_1_c_o), .s(add_2_s), .c_o(add_2_c_o));
  not not_3 (not_3_out, add_2_c_o);
  xor xor_1 (xor_1_out, add_1_s, not_3_out);
  xor xor_2 (xor_2_out, add_2_s, not_3_out);
  Add add_3 (.a(xor_1_out), .b(not_3_out), .c_i(1'b0), .s(y_0), .c_o(add_3_c_o));
  Add add_4 (.a(add_3_c_o), .b(xor_2_out), .c_i(1'b0), .s(y_1));  // open: c_o
endmodule

/* Test case absolute_difference:
a_1 a_0 b_1 b_0 y_1 y_0
loop(a, 4)
  loop(b,4)
    bits(2,a) bits(2,b) bits(2, ite(a > b, a-b, b-a))
  end loop
end loop
*/
