// Digital circuit abs_difference_multiplexer.dig as structural Verilog
module abs_difference_multiplexer (
  input  a_0,
  input  a_1,
  input  b_0,
  input  b_1,
  output y_0,
  output y_1
);

  wire add_1_c_o, not_4_out;
  wire [1:0] add_1_s, add_2_s, not_1_out, not_3_out;

  not not_1 (not_1_out[0], b_0);
  not not_2 (not_1_out[1], b_1);
  Add #(.Bits(2)) add_1 (.a({a_1, a_0}), .b(not_1_out), .c_i(1'b1), .s(add_1_s), .c_o(add_1_c_o));
  assign not_3_out = ~add_1_s;  // Not not_3, 2 bits wide
  not not_4 (not_4_out, add_1_c_o);
  Add #(.Bits(2)) add_2 (.a(not_3_out), .b(2'b00), .c_i(1'b1), .s(add_2_s));  // open: c_o
  Multiplexer #(.Bits(2)) multiplexer_1 (.sel(not_4_out), .in_0(add_1_s), .in_1(add_2_s), .out({y_1, y_0}));
endmodule

/* Test case absolute_difference:
a_1 a_0 b_1 b_0 y_1 y_0
loop(a, 4)
  loop(b,4)
    bits(2,a) bits(2,b) bits(2, ite(a > b, a-b, b-a))
  end loop
end loop
*/
