// Digital circuit abs_difference_mylsg_onlyAdder.dig as structural Verilog
module abs_difference_mylsg_onlyAdder (
  input  a0,
  input  a1,
  input  b0,
  input  b1,
  output y0,
  output y1
);

  wire add_1_c_o, add_2_c_o, add_2_s, and_1_out, not_1_out, not_2_out, not_3_out;

  not not_1 (not_1_out, b0);
  not not_2 (not_2_out, b1);
  Add add_1 (.a(a0), .b(not_1_out), .c_i(1'b1), .s(y0), .c_o(add_1_c_o));
  Add add_2 (.a(a1), .b(not_2_out), .c_i(add_1_c_o), .s(add_2_s), .c_o(add_2_c_o));
  not not_3 (not_3_out, add_2_c_o);
  and and_1 (and_1_out, y0, not_3_out);
  Add add_3 (.a(and_1_out), .b(add_2_s), .c_i(1'b0), .s(y1));  // open: c_o
endmodule
