// Digital circuit 2.1_pc.dig as structural Verilog
module _2_1_pc (
  input  Reset,
  input  Clk
);

  wire [31:0] multiplexer_1_out, PC_plus_4_s, PC_q;

  Multiplexer #(.Bits(32)) multiplexer_1 (.sel(Reset), .in_0(PC_plus_4_s), .in_1({32{1'b0}}), .out(multiplexer_1_out));
  Register #(.Bits(32), .isProgramCounter("true")) PC (.D(multiplexer_1_out), .C(Clk), .en(1'b1), .Q(PC_q));
  Add #(.Bits(32)) PC_plus_4 (.a(32'h4), .b(PC_q), .c_i(1'b0), .s(PC_plus_4_s));  // open: c_o
endmodule

/* Test case TestIncrReset:
Clk Reset PC
init PC=0;
0 0 0
repeat(10) C 0 (4*n+4)
C 1 0
*/

/* Test case TestOverflow:
Clk Reset PC
init PC=0xFFFFFFFF;
0 0 (0xFFFFFFFF)
C 0 (3)
*/
