// Digital circuit 2.2_extend.dig as structural Verilog
module _2_2_extend (
  input  [11:0] x12,
  output [31:0] x32
);

  BitExtender #(.inputBits(12), .outputBits(31)) sign_ext_12_31 (.in(x12), .out(x32[31:1]));

  assign x32[0] = 1'b0;
endmodule

/* Test case TestExtend:
x12 x32
let a=-10;
while(a < 10)
   let a=a+1;
   (a) (2*a)
end while
*/
