// Digital circuit 2.3_extend_pc.dig as structural Verilog
module _2_3_extend_pc (
  input  Reset,
  input  Clk,
  input  [11:0] offset,
  input  pcsrc
);

  wire [31:0] multiplexer_1_out, multiplexer_2_out, pc_extend_1_p2, PC_plus_4_s, PC_plus_offset_s, PC_q;

  Multiplexer #(.Bits(32)) multiplexer_1 (
    .sel(Reset), .in_0(multiplexer_2_out), .in_1({32{1'b0}}), .out(multiplexer_1_out));
  Register #(.Bits(32), .isProgramCounter("true")) PC (.D(multiplexer_1_out), .C(Clk), .en(1'b1), .Q(PC_q));
  // pc_extend pc_extend_1: pin names not known; wires that end beside it: offset, pc_extend_1_p2
  Add #(.Bits(32)) PC_plus_4 (.a(32'h4), .b(PC_q), .c_i(1'b0), .s(PC_plus_4_s));  // open: c_o
  Add #(.Bits(32)) PC_plus_offset (.a(PC_q), .b(pc_extend_1_p2), .c_i(1'b0), .s(PC_plus_offset_s));  // open: c_o
  Multiplexer #(.Bits(32)) multiplexer_2 (
    .sel(pcsrc), .in_0(PC_plus_4_s), .in_1(PC_plus_offset_s), .out(multiplexer_2_out));
endmodule

/* Test case TestIncr:
Clk Reset pcsrc offset PC
init PC=0;
0 0 0 0 0
repeat(10) C 0 0 0 (4*n+4)
*/

/* Test case TestOffset:
Clk Reset pcsrc offset PC
init PC=0;
0 0 1 (5) 0
let a = 0;
while(a < 100)
   let incr = a + 1;
   let a = a + 2*incr;
   C 0 1 (incr) (a)
end while
*/
