// Digital circuit PatternRecognizer_Musterlsg.dig as structural Verilog
module PatternRecognizer_Musterlsg (
  input  I,
  input  clk,
  output O
);

  wire and_1_out, and_2_out, FF0_q, FF1_q, not_1_out, not_2_out, or_1_out;

  not not_1 (not_1_out, I);
  not not_2 (not_2_out, FF0_q);
  and and_1 (and_1_out, FF0_q, not_1_out);
  and and_2 (and_2_out, not_2_out, FF1_q, I);
  and and_3 (O, FF0_q, FF1_q);
  or or_1 (or_1_out, and_1_out, and_2_out);
  D_FF FF1 (.D(or_1_out), .C(clk), .Q(FF1_q));  // open: nQ
  D_FF FF0 (.D(I), .C(clk), .Q(FF0_q));  // open: nQ
endmodule

/* Test case TestAutomat:
clk I FF1 FF0 O
init FF1=0;
init FF0=0;
0 0 0 0 0
C 0 0 0 0
C 1 0 1 0
C 1 0 1 0
C 0 1 0 0
C 0 0 0 0
C 1 0 1 0
C 0 1 0 0
C 1 1 1 1
C 0 1 0 0
C 1 1 1 1
C 1 0 1 0
*/
