// Digital circuit PatternRecognizer_Template.dig as structural Verilog
module PatternRecognizer_Template (
  input  I,
  input  clk,
  output O
);

  D_FF FF1 (.C(clk));  // open: D, Q, nQ
  D_FF FF0 (.C(clk));  // open: D, Q, nQ
endmodule

/* Test case TestAutomat:
clk I FF1 FF0 O
init FF1=0;
init FF0=0;
0 0 0 0 0
C 0 0 0 0
C 1 0 1 0
C 1 0 1 0
C 0 1 0 0
C 0 0 0 0
C 1 0 1 0
C 0 1 0 0
C 1 1 1 1
C 0 1 0 0
C 1 1 1 1
C 1 0 1 0
*/
